# Fritzing sketch placa_chassi (saved by Fritzing 0.9.3b)
circuit board: 9.90727cm x 7.41183cm

parts:
  US1 = hc-sr04
  US2 = hc-sr04
  US3 = hc-sr04
  US4 = hc-sr04
  US5 = hc-sr04
  US6 = hc-sr04
  US7 = hc-sr04
  US8 = hc-sr04
  J1 = female pin header, 12 pins [form="♀ (female)"]
  J3 = Power Jack [package=power_jack_pth]
  U1 = Voltage Regulator - 5V [package="TO220 [THT]"]
  J4 = female pin header, 2 pins [form="♀ (female)"]
  J5 = female pin header, 2 pins [form="♀ (female)"]
  J6 = female pin header, 2 pins [form="♀ (female)"]
  J7 = female pin header, 2 pins [form="♀ (female)"]
  J8 = female pin header, 2 pins [form="♀ (female)"]
  R1 = Resistor [tolerance=±5% resistance=220 package=THT]
  R2 = Resistor [tolerance=±5% resistance=220 package=THT]
  R3 = Resistor [tolerance=±5% resistance=220 package=THT]
  R4 = Resistor [tolerance=±5% resistance=220 package=THT]
  R5 = Resistor [tolerance=±5% resistance=220 package=THT]
  J9 = female pin header, 13 pins [form="♀ (female)"]  # not connected

nets:
  N1: US1.Echo, US2.Echo, US3.Echo, US4.Echo, US5.Echo, US6.Echo, US7.Echo, US8.Echo, U1.output_voltage, J4.pin1, J5.pin1, J6.pin1, J7.pin1, J8.pin1
  GND: US1.GND, US2.GND, US3.GND, US4.GND, US5.GND, US6.GND, US7.GND, US8.GND, J1.pin7, J1.pin8, J3.GND, U1.GND, R1.Pin_1, R2.Pin_1, R3.Pin_1, R4.Pin_1, R5.Pin_1
  N2: J1.pin1, J1.pin2
  N3: J1.pin3, J1.pin4
  N4: J1.pin5, J1.pin6, J3.PWR, U1.input_voltage
  N5: J1.pin9, J1.pin10
  N6: J1.pin11, J1.pin12
  N7: J4.pin2, R1.Pin_0
  N8: J5.pin2, R4.Pin_0
  N9: J6.pin2, R3.Pin_0
  N10: J7.pin2, R2.Pin_0
  N11: J8.pin2, R5.Pin_0
